// Logisim project FinalUniversalLogic.circ as structural Verilog: 1 circuit, main circuit main
module main (
  input  W,
  input  X,
  input  Y,
  input  Z
);

  wire nand_1_out, nand_2_out, nand_3_out, nand_4_out, nand_5_out, nand_6_out, nand_7_out, nand_8_out,
       nand_9_out, nand_10_out, nand_11_out, nand_12_out, nand_13_out, nand_14_out, nand_15_out, nand_16_out,
       nand_17_out, nand_18_out, nand_19_out, nand_20_out, nand_21_out, nand_22_out, nand_23_out,
       nand_24_out, nand_25_out, nand_26_out, nand_27_out, nand_28_out, nand_29_out, nand_30_out,
       nand_31_out, nand_32_out, nand_33_out, nand_34_out, nand_35_out, nand_36_out, nand_37_out,
       nand_38_out, nand_39_out, nand_40_out, nand_41_out, nand_42_out, nand_43_out, nand_44_out,
       nand_45_out, nand_46_out, nand_47_out, nand_48_out, nand_49_out, nand_50_out, nand_51_out,
       nand_52_out, nor_1_out, nor_2_out, nor_3_out, nor_4_out, nor_5_out, nor_6_out, nor_7_out, nor_8_out,
       nor_9_out, nor_10_out, nor_11_out, nor_12_out, nor_13_out, nor_14_out, nor_15_out, nor_16_out,
       nor_17_out, nor_18_out, nor_19_out, nor_20_out, nor_21_out, nor_22_out, nor_23_out, nor_24_out,
       nor_25_out, nor_26_out, nor_27_out, nor_28_out, nor_29_out, nor_30_out, nor_31_out, nor_32_out;

  nand nand_1 (nand_1_out, W, W);
  nand nand_2 (nand_2_out, X, X);
  nand nand_3 (nand_3_out, Y, Y);
  nand nand_4 (nand_4_out, Z, Z);
  nand nand_5 (nand_5_out, X, nand_4_out);
  nand nand_6 (nand_6_out, nand_3_out, nand_4_out);
  nand nand_7 (nand_7_out, nand_2_out, nand_3_out);
  nand nand_8 (nand_8_out, W, nand_4_out);
  nand nand_9 (nand_9_out, nand_1_out, Z);
  nand nand_10 (nand_10_out, X, Y);
  nand nand_11 (nand_11_out, nand_5_out, nand_5_out);
  nand nand_12 (nand_12_out, nand_6_out, nand_6_out);
  nand nand_13 (nand_13_out, nand_7_out, nand_7_out);
  nand nand_14 (nand_14_out, nand_8_out, nand_8_out);
  nand nand_15 (nand_15_out, nand_9_out, nand_9_out);
  nand nand_16 (nand_16_out, nand_10_out, nand_10_out);
  nand nand_17 (nand_17_out, nand_1_out, X);
  nand nand_18 (nand_18_out, nand_17_out, nand_17_out);
  nand nand_19 (nand_19_out, W, nand_12_out);
  nand nand_20 (nand_20_out, nand_19_out, nand_19_out);
  nand nand_21 (nand_21_out, nand_2_out, nand_3_out, Z);
  nand nand_22 (nand_22_out, nand_21_out, nand_21_out);
  nand nand_23 (nand_23_out, nand_24_out, nand_24_out);
  nand nand_24 (nand_24_out, W, nand_13_out);
  nand nand_25 (nand_25_out, nand_26_out, nand_26_out);
  nand nand_26 (nand_26_out, nand_12_out, nand_1_out);
  nand nand_27 (nand_27_out, nand_28_out, nand_28_out);
  nand nand_28 (nand_28_out, Y, nand_14_out);
  nand nand_29 (nand_29_out, nand_30_out, nand_30_out);
  nand nand_30 (nand_30_out, nand_13_out, W, Z);
  nand nand_31 (nand_31_out, nand_32_out, nand_32_out);
  nand nand_32 (nand_32_out, nand_1_out, X);
  nand nand_33 (nand_33_out, nand_1_out, Y);
  nand nand_34 (nand_34_out, nand_33_out, nand_33_out);
  nand nand_35 (nand_35_out, W, nand_12_out);
  nand nand_36 (nand_36_out, nand_35_out, nand_35_out);
  nand nand_37 (nand_37_out, W, nand_13_out);
  nand nand_38 (nand_38_out, nand_37_out, nand_37_out);
  nand nand_39 (nand_39_out, nand_1_out, nand_3_out);
  nand nand_40 (nand_40_out, nand_39_out, nand_39_out);
  nand nand_41 (nand_41_out, nand_1_out, nand_2_out);
  nand nand_42 (nand_42_out, nand_41_out, nand_41_out);
  nand nand_43 (nand_43_out, nand_44_out, nand_44_out);
  nand nand_44 (nand_44_out, nand_2_out, nand_12_out);
  nand nand_45 (nand_45_out, nand_46_out, nand_46_out);
  nand nand_46 (nand_46_out, W, nand_16_out);
  nand nand_47 (nand_47_out, nand_48_out, nand_48_out);
  nand nand_48 (nand_48_out, nand_16_out, nand_4_out);
  nand nand_49 (nand_49_out, nand_50_out, nand_50_out);
  nand nand_50 (nand_50_out, W, nand_3_out);
  nand nand_51 (nand_51_out, W, Z);
  nand nand_52 (nand_52_out, nand_51_out, nand_51_out);
  nor nor_1 (nor_1_out, nor_2_out, nor_2_out);
  nor nor_2 (nor_2_out, nand_18_out, nand_11_out);
  nor nor_3 (nor_3_out, nor_4_out, nor_4_out);
  nor nor_4 (nor_4_out, nand_20_out, nand_22_out);
  nor nor_5 (nor_5_out, nand_12_out, nand_23_out, nand_14_out);
  nor nor_6 (nor_6_out, nor_5_out, nor_5_out);
  nor nor_7 (nor_7_out, nand_11_out, nand_25_out);
  nor nor_8 (nor_8_out, nor_7_out, nor_7_out);
  nor nor_9 (nor_9_out, nor_10_out, nor_10_out);
  nor nor_10 (nor_10_out, nand_27_out, nand_29_out);
  nor nor_11 (nor_11_out, nor_12_out, nor_12_out);
  nor nor_12 (nor_12_out, nand_31_out, nand_34_out, nand_15_out);
  nor nor_13 (nor_13_out, nand_36_out, nand_38_out, nand_16_out);
  nor nor_14 (nor_14_out, nor_13_out, nor_13_out);
  nor nor_15 (nor_15_out, nand_40_out, nand_42_out, nand_15_out);
  nor nor_16 (nor_16_out, nor_15_out, nor_15_out);
  nor nor_17 (nor_17_out, nand_43_out, nand_45_out);
  nor nor_18 (nor_18_out, nor_17_out, nor_17_out);
  nor nor_19 (nor_19_out, nor_20_out, nor_20_out);
  nor nor_20 (nor_20_out, nand_13_out, nand_16_out, nand_49_out);
  nor nor_21 (nor_21_out, nor_1_out, nor_3_out);
  nor nor_22 (nor_22_out, nor_8_out, nor_9_out);
  nor nor_23 (nor_23_out, nor_11_out, nor_14_out);
  nor nor_24 (nor_24_out, nor_16_out, nor_18_out);
  nor nor_25 (nor_25_out, nand_47_out, nand_1_out);
  nor nor_26 (nor_26_out, nor_19_out, nand_52_out);
  nor nor_27 (nor_27_out, nor_21_out, nor_21_out);
  nor nor_28 (nor_28_out, nor_22_out, nor_22_out);
  nor nor_29 (nor_29_out, nor_23_out, nor_23_out);
  nor nor_30 (nor_30_out, nor_24_out, nor_24_out);
  nor nor_31 (nor_31_out, nor_25_out, nor_25_out);
  nor nor_32 (nor_32_out, nor_26_out, nor_26_out);
  _7_Segment_Display u_7_segment_display_1 (
    .g(nor_32_out), .f(nor_31_out), .a(nor_27_out), .b(nor_6_out), .e(nor_30_out), .d(nor_29_out),
    .c(nor_28_out));  // open: dp

  // Notes on the sheet:
  //   T6
  //   T1
  //   T3
  //   T5
  //   T4
  //   T2
  //   a
  //   b
  //   c
  //   d
  //   e
  //   f
  //   g
endmodule
