// Logisim project multiplexar.circ as structural Verilog: 1 circuit, main circuit main
module main (
  input  in_1,
  input  Z,
  input  in_3,
  input  [2:0] in_4
);

  wire multiplexer_1_out, multiplexer_2_out, multiplexer_3_out, multiplexer_4_out, multiplexer_5_out,
       multiplexer_6_out, multiplexer_7_out, not_1_out;

  not not_1 (not_1_out, in_3);
  Multiplexer #(.select(3)) multiplexer_1 (
    .in0(in_3), .in1(in_1), .in2(Z), .in3(Z), .in4(Z), .in5(in_1), .in6(not_1_out), .in7(not_1_out),
    .out(multiplexer_1_out), .sel(in_4), .en(Z));
  Multiplexer #(.select(3)) multiplexer_2 (
    .in0(not_1_out), .in1(in_1), .in2(not_1_out), .in3(in_1), .in4(Z), .in5(not_1_out), .in6(not_1_out),
    .in7(not_1_out), .out(multiplexer_2_out), .sel(in_4), .en(Z));
  Multiplexer #(.select(3)) multiplexer_3 (
    .in0(not_1_out), .in1(in_1), .in2(not_1_out), .in3(not_1_out), .in4(in_3), .in5(not_1_out),
    .in6(not_1_out), .in7(not_1_out), .out(multiplexer_3_out), .sel(in_4), .en(Z));
  Multiplexer #(.select(3)) multiplexer_4 (
    .in0(in_3), .in1(Z), .in2(Z), .in3(Z), .in4(Z), .in5(in_1), .in6(not_1_out), .in7(not_1_out),
    .out(multiplexer_4_out), .sel(in_4), .en(Z));
  Multiplexer #(.select(3)) multiplexer_5 (
    .in0(Z), .in1(Z), .in2(Z), .in3(in_3), .in4(not_1_out), .in5(in_1), .in6(in_1), .in7(not_1_out),
    .out(multiplexer_5_out), .sel(in_4), .en(Z));
  Multiplexer #(.select(3)) multiplexer_6 (
    .in0(Z), .in1(Z), .in2(Z), .in3(Z), .in4(in_1), .in5(in_1), .in6(in_1), .in7(not_1_out),
    .out(multiplexer_6_out), .sel(in_4), .en(Z));
  Multiplexer #(.select(3)) multiplexer_7 (
    .in0(Z), .in1(in_1), .in2(in_1), .in3(Z), .in4(Z), .in5(in_3), .in6(Z), .in7(not_1_out),
    .out(multiplexer_7_out), .sel(in_4), .en(Z));
  _7_Segment_Display u_7_segment_display_1 (
    .g(multiplexer_7_out), .f(multiplexer_6_out), .a(multiplexer_1_out), .b(multiplexer_2_out),
    .e(multiplexer_5_out), .d(multiplexer_4_out), .c(multiplexer_3_out));  // open: dp
endmodule
